# Fritzing sketch 4_Digit_7_Segment (saved by Fritzing 0.9.3b)
breadboards: 1

parts:
  Componente1 = Arduino Uno (Rev3)
  LED1 = 7-SEGMENT-4DIGIT-YOUNGSUN [package=7-segment-4digit-youngsun]
  R1 = Resistor [tolerance=±5% resistance=1k package=THT]
  R2 = Resistor [tolerance=±5% resistance=1k package=THT]
  R3 = Resistor [tolerance=±5% resistance=1k package=THT]
  R4 = Resistor [tolerance=±5% resistance=1k package=THT]

nets:
  N1: Componente1.D8, LED1.C
  N2: Componente1.D9_PWM, LED1.A
  N3: Componente1.D10_PWM/SS, R1.Pin_0
  N4: Componente1.D11_PWM/MOSI, R2.Pin_0
  N5: Componente1.D12/MISO, R3.Pin_0
  N6: Componente1.D13/SCK, R4.Pin_0
  N7: Componente1.D2, LED1.APOS-A
  N8: Componente1.D3_PWM, LED1.E
  N9: Componente1.D4, LED1.COL-A
  N10: Componente1.D5_PWM, LED1.D
  N11: Componente1.D6_PWM, LED1.DIG2
  N12: Componente1.D7, LED1.DIG3
  N13: LED1.DP, R4.Pin_1
  N14: LED1.F, R3.Pin_1
  N15: LED1.COL-C, R2.Pin_1
  N16: LED1.G, R1.Pin_1

notes:
  1K Ω
