# Fritzing sketch AutoUltrasonicCar (saved by Fritzing 0.9.3b)
breadboards: 1

parts:
  Componente1 = Arduino Nano (Rev3.0)
  hc-sr1 = hc-sr04
  L298N1 = L298N DC motor driver
  S1 = SWITCH-MOMENTARY-2 [package=tactile-switch-1101ne]
  Power_plug1 = Power plug
  M1 = DC Motor
  M2 = DC Motor

nets:
  GND: Componente1.GND, hc-sr1.GND, L298N1.GND, Power_plug1.GND
  N1: Componente1.D4, hc-sr1.Trig
  N2: Componente1.D5, hc-sr1.Echo
  N3: Componente1.D6, L298N1.IN1
  N4: Componente1.D7, L298N1.IN2
  N5: Componente1.D8, L298N1.IN3
  N6: Componente1.D9, L298N1.IN4
  VIN: Componente1.VIN, hc-sr1.VCC, L298N1.12V, S1.2
  N7: L298N1.OUT1, M2.pin_2
  N8: L298N1.OUT2, M2.pin_1
  N9: L298N1.OUT3, M1.pin_2
  N10: L298N1.OUT4, M1.pin_1
  N11: L298N1.5V#9, L298N1.ENA
  N12: L298N1.5V#10, L298N1.ENB
  N13: S1.1, Power_plug1.VCC

custom parts:
  L298N DC motor driver: 2x DC motor driver with 78M05 positive voltage regulator (7..35 V) L298N: max 46 V, 2 A Set 5 V Enable jumper to enable 5 V regultor (needed for the L298N) and +5 V output at screw terminal or supply external +5 V at screw terminal Set ENA and/or ENB to +5 V to enable motor permanently or supply ENA and/or ENB with PWM signal IN1 and IN2 set rotation directory for motor A (OUT1/OUT2) IN2 and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
