# Fritzing sketch Obstacle_Avoidance_Sensor (saved by Fritzing 0.9.3b)
breadboards: 1

parts:
  Componente1 = Arduino Uno (Rev3)
  Part1 = KY-012 Active Buzzer Module [package="Breakout board"]
  LED1 = LED - 3mm [color="Red (633nm)" package="3 mm [THT]"]
  LED2 = LED - 3mm [color="Green (555nm)" package="3 mm [THT]"]
  M1 = fc-51 [package=THT]

nets:
  N1: Componente1.D2, M1.pin1
  N2: Componente1.D3_PWM, LED2.anode
  N3: Componente1.D4, LED1.anode
  N4: Componente1.D5_PWM, Part1.S
  N5: Componente1.5V, M1.pin3
  N6: Componente1.GND, Part1.-, LED1.cathode, LED2.cathode, M1.pin2

custom parts:
  KY-012 Active Buzzer Module: Active Piezoelectric Buzzer Module Keyes KY-012, it produces single-tone sound when signal is high.
