# Fritzing sketch Tilt (saved by Fritzing 0.9.3b)
breadboards: 1

parts:
  Componente1 = Arduino Uno (Rev3)
  Part1 = KY-012 Active Buzzer Module [package="Breakout board"]
  U1 = Keyes Tilt Switch [package=THT]

nets:
  N1: Componente1.D6_PWM, Part1.S
  N2: Componente1.D7, U1.power
  N3: Componente1.5V, U1.signal
  N4: Componente1.GND, Part1.-, U1.ground

custom parts:
  KY-012 Active Buzzer Module: Active Piezoelectric Buzzer Module Keyes KY-012, it produces single-tone sound when signal is high.
  Keyes Tilt Switch: Keyes Tilt Switch Sensor Module for Arduino (Works with Official Arduino Boards). Working voltage: 3.3V~5V; digital switch output (0 & 1); High sensitivity.
